# Fritzing sketch 02_led (saved by Fritzing 0.9.3b)
breadboards: 1

parts:
  Part1 = Arduino Nano (Rev3.0)
  LED2 = LED - 5mm [color="Red (633nm)" package="5 mm [THT]"]
  R2 = Resistor [tolerance=±5% resistance=220 package=THT]

nets:
  N1: Part1.GND, R2.Pin_0
  N2: Part1.D2, LED2.anode
  N3: LED2.cathode, R2.Pin_1
