# Fritzing sketch 03_2xLED (saved by Fritzing 0.9.3b)
breadboards: 1

parts:
  Part1 = Arduino Nano (Rev3.0)
  R1 = Resistor [tolerance=±5% resistance=220 package=THT]
  R2 = Resistor [tolerance=±5% resistance=220 package=THT]
  LED1 = LED - 5mm [color="Orange (620nm)" package="5 mm [THT]"]
  LED2 = LED - 5mm [color="Blue (430nm)" package="5 mm [THT]"]

nets:
  N1: Part1.GND, LED1.cathode, LED2.cathode
  N2: Part1.D2, R2.Pin_1
  N3: Part1.D3, R1.Pin_1
  N4: R1.Pin_0, LED2.anode
  N5: R2.Pin_0, LED1.anode
