# Fritzing sketch 04_RGB (saved by Fritzing 0.9.3b)
breadboards: 1

parts:
  Part1 = Arduino Nano (Rev3.0)  # not connected
  R1 = Resistor [tolerance=±5% resistance=220 package=THT]
  R2 = Resistor [tolerance=±5% resistance=220 package=THT]
  R3 = Resistor [tolerance=±5% resistance=220 package=THT]
  LED1 = RGB LED - (4 legs) [package="5 mm [THT]"]

nets:
  N1: R1.Pin_1, LED1.blue_cathode
  N2: R2.Pin_1, LED1.common_anode
  N3: R3.Pin_1, LED1.red_cathode
