# Fritzing sketch 07_photo_resistor_LED (saved by Fritzing 0.9.3b)
breadboards: 1

parts:
  Part1 = Arduino Nano (Rev3.0)
  R3 = Resistor [tolerance=±5% resistance=1k package=THT]
  R4 = Photocell (LDR) [package=THT]
  R5 = Resistor [tolerance=±5% resistance=220 package=THT]
  LED1 = LED - 5mm [color="Red (633nm)" package="5 mm [THT]"]

nets:
  N1: Part1.GND, R3.Pin_0, LED1.cathode
  N2: Part1.D3, R5.Pin_0
  N3: Part1.5V, R4.pin_0
  N4: R3.Pin_1, R4.pin_1
  N5: R5.Pin_1, LED1.anode
