# Fritzing sketch 08_photo_resistor (saved by Fritzing 0.9.3b)
breadboards: 1

parts:
  Part1 = Arduino Nano (Rev3.0)
  R3 = Resistor [tolerance=±5% resistance=1k package=THT]
  R4 = Photocell (LDR) [package=THT]

nets:
  N1: Part1.GND, R3.Pin_0
  N2: Part1.5V, R4.pin_0
  N3: Part1.A7, R3.Pin_1, R4.pin_1
